// Logisim project Task1circuit.circ as structural Verilog: 1 circuit, main circuit main
module main (
  input  A,
  input  B,
  input  C,
  output out_4
);

  wire and_1_out, and_2_out, not_1_out;

  not not_1 (not_1_out, B);
  and and_1 (and_1_out, A, not_1_out);
  and and_2 (and_2_out, B, C);
  or or_1 (out_4, and_1_out, and_2_out);
endmodule
