// Logisim project Task3circuit.circ as structural Verilog: 1 circuit, main circuit main
module main (
  input  [3:0] in_1,
  input  in_2,
  output [3:0] out_3
);

  wire clock_1_out, d_ff_1_qn, d_ff_2_qn, d_ff_3_qn, d_ff_4_qn, multiplexer_1_out, multiplexer_2_out,
       multiplexer_3_out, multiplexer_4_out;

  Clock clock_1 (.out(clock_1_out));
  Multiplexer multiplexer_1 (.in0(d_ff_1_qn), .in1(in_1[0]), .out(multiplexer_1_out), .sel(in_2));
  Multiplexer multiplexer_2 (.in0(d_ff_2_qn), .in1(in_1[1]), .out(multiplexer_2_out), .sel(in_2));
  Multiplexer multiplexer_3 (.in0(d_ff_3_qn), .in1(in_1[2]), .out(multiplexer_3_out), .sel(in_2));
  Multiplexer multiplexer_4 (.in0(d_ff_4_qn), .in1(in_1[3]), .out(multiplexer_4_out), .sel(in_2));
  D_Flip_Flop d_ff_1 (.D(multiplexer_1_out), .clk(clock_1_out), .Q(out_3[0]), .Qn(d_ff_1_qn));  // open: preset, reset
  D_Flip_Flop d_ff_2 (.D(multiplexer_2_out), .clk(clock_1_out), .Q(out_3[1]), .Qn(d_ff_2_qn));  // open: preset, reset
  D_Flip_Flop d_ff_3 (.D(multiplexer_3_out), .clk(clock_1_out), .Q(out_3[2]), .Qn(d_ff_3_qn));  // open: preset, reset
  D_Flip_Flop d_ff_4 (.D(multiplexer_4_out), .clk(clock_1_out), .Q(out_3[3]), .Qn(d_ff_4_qn));  // open: preset, reset
endmodule
