// Logisim project Task4circuit.circ as structural Verilog: 1 circuit, main circuit main
module main (
  input  C,
  output [1:0] out_2
);

  wire and_1_out, and_2_out, and_3_out, and_4_out, and_5_out, and_6_out, clock_1_out, not_1_out, or_1_out,
       or_2_out;

  Clock clock_1 (.out(clock_1_out));
  D_Flip_Flop d_ff_1 (.D(or_2_out), .clk(clock_1_out), .Q(out_2[0]));  // open: Qn, preset, reset
  D_Flip_Flop d_ff_2 (.D(or_1_out), .clk(clock_1_out), .Q(out_2[1]));  // open: Qn, preset, reset
  not not_1 (not_1_out, out_2[0]);
  and and_1 (and_1_out, out_2[1], out_2[0]);
  and and_2 (and_2_out, C, out_2[0]);
  and and_3 (and_3_out, out_2[1], C);
  and and_4 (and_4_out, C, not_1_out);
  and and_5 (and_5_out, C, out_2[1]);
  and and_6 (and_6_out, not_1_out, out_2[1]);
  or or_1 (or_1_out, and_1_out, and_2_out, and_3_out);
  or or_2 (or_2_out, and_4_out, and_5_out, and_6_out);
endmodule
